# Fritzing sketch Mach_update (saved by Fritzing 0.9.3b)

parts:
  U1 = ESP32S-HiLetgo [part_number=ESP32S-HiLetgo]
  ESP32_-_Back1 = ESP32 - CAM  # not connected
  PWM1 = PCA9685 16x12-bit PWM Breakout
  J1 = Basic Servo
  J2 = Basic Servo
  J3 = Basic Servo
  J4 = Basic Servo
  LED1 = LED - 3mm [color="Red (633nm)" package="3 mm [THT]"]
  LED2 = LED - 3mm [color="Red (633nm)" package="3 mm [THT]"]
  LED3 = LED - 3mm [color="Red (633nm)" package="3 mm [THT]"]
  Linh_kiện1 = MQ-4
  VCC1 = Battery block 9V  # not connected
  WATER_PUMP1 = water pump/motor  # not connected
  DHT1 = Humidity and Temperature Sensor DHT11
  Linh_kiện2 = SRF05 Ultrasonic Rangefinder

nets:
  N1: U1.3.3, PWM1.no_name_yet#605
  N2: U1.GPIO34, DHT1.Data-signal
  N3: U1.GPIO32, LED3.anode
  N4: U1.GPIO33, LED2.anode
  N5: U1.GPIO25, LED1.anode
  N6: U1.GND, LED3.cathode
  N7: U1.GPIO7, PWM1.no_name_yet#604
  N8: U1.GPIO8, PWM1.no_name_yet#603
  N9: U1.GPIO17, Linh_kiện1.AO
  N10: U1.GPIO18, Linh_kiện2.Echo
  N11: U1.GPIO19, Linh_kiện2.Trig
  N12: PWM1.no_name_yet#0, J1.pulse
  N13: PWM1.no_name_yet#1, J2.pulse
  N14: PWM1.no_name_yet#2, J3.pulse
  N15: PWM1.no_name_yet#3, J4.pulse
  VCC: PWM1.no_name_yet#100, PWM1.no_name_yet#101, PWM1.no_name_yet#102, PWM1.no_name_yet#103, J1.vcc, J2.vcc, J3.vcc, J4.vcc
  GND: PWM1.no_name_yet#601, PWM1.no_name_yet#1000, PWM1.no_name_yet#1001, PWM1.no_name_yet#1002, PWM1.no_name_yet#1003, J1.gnd, J2.gnd, J3.gnd, J4.gnd

notes:
  Both ESPs are powered by computer's USB ports
  Water pump

custom parts:
  ESP32S-HiLetgo: HiLetgo ESP-WROOM-32 ESP32 ESP-32S Development Board 2.4GHz Dual-Mode WiFi + Bluetooth Dual Cores Microcontroller The ESP32 integrated with Antenna switches, RF Balun, power amplifiers, low-noise amplifiers, filters, and management modules, and the entire solution occupies the least area of PCB. 2.4 GHz Wi-Fi plus Bluetooth dual-mode chip, with TSMC Ultra-low power consumption 40nm technology,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
  ESP32 - CAM: The ESP32-CAM has a very competitive small-size camera module that can operate independently as a minimum system with a footprint of only 27*40.5*4.5mm and a deep sleep current of up to 6mA.
  water pump/motor: WATER PUMP BY ARDUBLOCKTR
  Humidity and Temperature Sensor DHT11: Digital relative humidity & temperature sensor DHT11
